# Fritzing sketch Circuits (saved by Fritzing 0.9.3b)
breadboards: 1

parts:
  元件1 = HC-SR501 Body Sensor Module
  WeMos_D1_R1 = WeMos D1 R2
  DHT1 = DHT22 Humidity and Temperature Sensor
  元件2 = MQ-7 breakout
  U1 = 2-Channel 5v Relay Shield [package=relay-2ch5v10a]
  PSU1 = Adjustable Breadboard Power Supply

nets:
  VCC: 元件1.VCC, DHT1.VDD, 元件2.VCC, U1.VCC, PSU1.Vout+
  N1: 元件1.OUT, WeMos_D1_R1.D3
  GND: 元件1.GND, WeMos_D1_R1.GND, DHT1.GND, 元件2.GND, U1.GND, PSU1.Vout-
  N2: WeMos_D1_R1.D2, DHT1.DATA
  N3: WeMos_D1_R1.D4, U1.IN2
  N4: WeMos_D1_R1.A0, 元件2.AO

custom parts:
  HC-SR501 Body Sensor Module: Pyroelectric Infrared PIR Motion Sensor Detector Module
  WeMos D1 R2: The D1 R2 is a mini wifi board based on the ESP-8266EX.
  MQ-7 breakout: SKU: 101282
  2-Channel 5v Relay Shield: 2 Channel 5v Relay Shield w. 2x SPD-06VDC-SD-C
